# Fritzing sketch 317-SEMAFOR_ZA_AUTOMOBILE_I_PJESAKE (saved by Fritzing 0.9.0b)
breadboards: 1

parts:
  Part1 = Arduino Uno (Rev3)
  R1 = Resistor [tolerance=±5% resistance=330 package=THT]
  LED1 = LED - 5mm [color="Red (635nm)" package="5 mm [THT]"]
  R2 = Resistor [tolerance=±5% resistance=330 package=THT]
  LED2 = LED - 5mm [color="Yellow (585nm)" package="5 mm [THT]"]
  R3 = Resistor [tolerance=±5% resistance=330 package=THT]
  LED3 = LED - 5mm [color="Green (555nm)" package="5 mm [THT]"]
  LED4 = LED - 5mm [color="Red (635nm)" package="5 mm [THT]"]
  LED5 = LED - 5mm [color="Green (555nm)" package="5 mm [THT]"]
  R4 = Resistor [tolerance=±5% resistance=330 package=THT]
  R5 = Resistor [tolerance=±5% resistance=330 package=THT]

nets:
  N1: Part1.GND, LED1.cathode, LED2.cathode, LED3.cathode, LED4.cathode, LED5.cathode
  N2: Part1.D2, R1.Pin_0
  N3: Part1.D3_PWM, R2.Pin_0
  N4: Part1.D4, R3.Pin_0
  N5: Part1.D5_PWM, R4.Pin_0
  N6: Part1.D6_PWM, R5.Pin_0
  N7: R1.Pin_1, LED1.anode
  N8: R2.Pin_1, LED2.anode
  N9: R3.Pin_1, LED3.anode
  N10: LED4.anode, R4.Pin_1
  N11: LED5.anode, R5.Pin_1
