# Fritzing sketch 411-412-418-OSNOVNI_RAD_TIPKALA (saved by Fritzing 0.9.0b)
breadboards: 1

parts:
  Part1 = Arduino Uno (Rev3)
  R1 = Resistor [tolerance=±5% resistance=330 package=THT]
  LED1 = LED - 5mm [color="Red (635nm)" package="5 mm [THT]"]
  S1 = Momentary Switch [package=ksa_sealed_tac_switch]

nets:
  N1: Part1.D2, R1.Pin_0
  N2: Part1.D3_PWM, S1.1
  N3: Part1.GND, LED1.cathode, S1.4
  N4: R1.Pin_1, LED1.anode
